# Fritzing sketch gyronacc_with_bluetooth_lcd_Arduino (saved by Fritzing 0.9.3b)
breadboards: 1

parts:
  Part1 = Arduino Uno (Rev3)
  LCD1 = LCD screen
  U1 = POT [package=pot_mammoth]
  GY1 = MPU-6050 Board GY-521 [form="♀ (female)" package=THT]
  Part2 = Bluetooth HC-05 Macho
  R1 = Resistor [tolerance=±5% resistance=220 package="0805 [SMD]"]
  R2 = Resistor [tolerance=±5% resistance=220 package="0805 [SMD]"]

nets:
  N1: Part1.A4/SDA, GY1.pin4
  N2: Part1.A5/SCL, GY1.pin3
  N3: Part1.D8, LCD1.RS
  N4: Part1.D9_PWM, LCD1.E
  N5: Part1.D10_PWM/SS, LCD1.DB4
  N6: Part1.D11_PWM/MOSI, LCD1.DB5
  N7: Part1.D12/MISO, LCD1.DB6
  N8: Part1.D13/SCK, LCD1.DB7
  N9: Part1.D2, R1.Pin_0
  N10: LCD1.VDD, U1.S
  N11: LCD1.V0, U1.A
  N12: Part2.GND, R2.Pin_1
  N13: R1.Pin_1, R2.Pin_0

custom parts:
  MPU-6050 Board GY-521: Acelerometro y Giroscopio MPU-6050 Board GY-521
